// Logisim project CPU Proto1.circ as structural Verilog
module Active_Low_SR_Latch (
  input  s,
  input  r,
  output Q,
  output NQ
);

  nand nand_1 (Q, s, NQ);
  nand nand_2 (NQ, Q, r);
endmodule

module Active_High_SR_Latch_w__Enable (
  input  s,
  input  E,
  output Q,
  output NQ
);

  wire nand_1_out, nand_2_out, not_1_out;

  not not_1 (not_1_out, s);
  nand nand_1 (nand_1_out, s, E);
  nand nand_2 (nand_2_out, E, not_1_out);
  nand nand_3 (Q, nand_1_out, NQ);
  nand nand_4 (NQ, Q, nand_2_out);
endmodule

module MEM_1 (
  input  s,
  input  E,
  output Q
);

  wire nand_1_out, nand_2_out, nand_4_out;

  nand nand_1 (nand_1_out, s, E);
  nand nand_2 (nand_2_out, nand_1_out, E);
  nand nand_3 (Q, nand_1_out, nand_4_out);
  nand nand_4 (nand_4_out, Q, nand_2_out);
endmodule

module MEM_8 (
  input  [7:0] \input ,
  input  enable,
  output [7:0] out_3
);

  MEM_1 mem_1_1 (.s(\input [0]), .E(enable), .Q(out_3[0]));
  MEM_1 mem_1_2 (.s(\input [1]), .E(enable), .Q(out_3[1]));
  MEM_1 mem_1_3 (.s(\input [2]), .E(enable), .Q(out_3[2]));
  MEM_1 mem_1_4 (.s(\input [3]), .E(enable), .Q(out_3[3]));
  MEM_1 mem_1_5 (.s(\input [4]), .E(enable), .Q(out_3[4]));
  MEM_1 mem_1_6 (.s(\input [5]), .E(enable), .Q(out_3[5]));
  MEM_1 mem_1_7 (.s(\input [6]), .E(enable), .Q(out_3[6]));
  MEM_1 mem_1_8 (.s(\input [7]), .E(enable), .Q(out_3[7]));
endmodule

module CPU_ENABLE (
  input  [7:0] \input ,
  input  enable,
  output [7:0] out_3
);

  and and_1 (out_3[0], \input [0], enable);
  and and_2 (out_3[1], \input [1], enable);
  and and_3 (out_3[2], \input [2], enable);
  and and_4 (out_3[3], \input [3], enable);
  and and_5 (out_3[4], \input [4], enable);
  and and_6 (out_3[5], \input [5], enable);
  and and_7 (out_3[6], \input [6], enable);
  and and_8 (out_3[7], \input [7], enable);
endmodule

module REG_8 (
  input  [7:0] i,
  input  set,
  input  enable,
  output [7:0] o
);

  wire [7:0] mem_8_1_out_3;

  MEM_8 mem_8_1 (.\input (i), .out_3(mem_8_1_out_3), .enable(set));
  CPU_ENABLE cpu_enable_1 (.\input (mem_8_1_out_3), .out_3(o), .enable(enable));
endmodule
